// Logisim project design.circ as structural Verilog: 1 circuit, main circuit main
module main (
  output [7:0] DATA_OUTPUT
);

  wire clock_1_out, decoder_1_out0, decoder_1_out1, not_1_out, not_2_out;

  not not_1 (not_1_out, 1'b1);
  not not_2 (not_2_out, 1'b0);
  Decoder decoder_1 (.out0(decoder_1_out0), .out1(decoder_1_out1), .sel(1'b1), .en(not_2_out));
  RAM #(.addrWidth(12), .dataWidth(4)) ram_1 (
    .addr({12{1'b0}}), .data(DATA_OUTPUT[3:0]), .sel(decoder_1_out1), .clk(clock_1_out), .ld(1'b1),
    .clr(not_1_out));
  RAM #(.addrWidth(12), .dataWidth(4)) ram_2 (
    .addr({12{1'b0}}), .data(DATA_OUTPUT[7:4]), .sel(decoder_1_out1), .clk(clock_1_out), .ld(1'b1),
    .clr(not_1_out));
  Clock clock_1 (.out(clock_1_out));
  RAM #(.addrWidth(12)) ram_3 (
    .addr({12{1'b0}}), .data(DATA_OUTPUT), .sel(decoder_1_out0), .clk(clock_1_out), .ld(1'b1), .clr(not_1_out));
endmodule
